# Fritzing sketch QuizBuzzerSystem (saved by Fritzing 1.0.3b)

parts:
  Part1 = Arduino Nano (Rev3.0)
  BUTTON1 = Arcade Button (red)
  BUTTON2 = Arcade Button (blue)
  BUTTON3 = Arcade Button (green)
  BUTTON4 = Arcade Button (yellow)
  R1 = Resistor [tolerance=±5% resistance=220 package="0805 [SMD]"]
  LED1 = LED - 5mm [color="White (4500K)" current=0.030A package="5 mm [THT]"]
  R2 = Resistor [tolerance=±5% resistance=220 package="0805 [SMD]"]
  LED2 = LED - 5mm [color="White (4500K)" current=0.030A package="5 mm [THT]"]
  R3 = Resistor [tolerance=±5% resistance=220 package="0805 [SMD]"]
  LED3 = LED - 5mm [color="White (4500K)" current=0.030A package="5 mm [THT]"]
  R4 = Resistor [tolerance=±5% resistance=220 package="0805 [SMD]"]
  LED4 = LED - 5mm [color="White (4500K)" current=0.030A package="5 mm [THT]"]
  S1 = Square Pushbutton
  S2 = Square Pushbutton
  J21 = female pin header, 10 pins [form="♀ (female)"]
  J22 = female pin header, 2 pins [form="♀ (female)"]  # not connected
  SPKR2 = Loudspeaker  # not connected
  JACK3 = 2.1mm Barrel Jack with Terminal Block
  J23 = female pin header, 2 pins [form="♀ (female)"]

nets:
  N1: Part1.GND, BUTTON1.no_name_yet#2, BUTTON2.no_name_yet#2, BUTTON3.no_name_yet#2, BUTTON4.no_name_yet#2, LED1.cathode, LED2.cathode, LED3.cathode, LED4.cathode, S1.leg0, S2.leg0, J21.pin10, JACK3.NEG, J23.pin1
  N2: Part1.D2, R4.Pin_1
  N3: Part1.D3, R3.Pin_1
  N4: Part1.D4, R2.Pin_1
  N5: Part1.D5, R1.Pin_1
  N6: Part1.D8, J21.pin1
  N7: Part1.D9, J21.pin2
  N8: Part1.5V, JACK3.POS, J23.pin2
  N9: Part1.A5, S2.leg1
  N10: Part1.A4, S1.leg1
  N11: Part1.A3, BUTTON1.no_name_yet#1
  N12: Part1.A2, BUTTON4.no_name_yet#1
  N13: Part1.A1, BUTTON3.no_name_yet#1
  N14: Part1.A0, BUTTON2.no_name_yet#1

notes:
  Is this capacitor the right way round?
  Buttons connected to pins A0 - A3 and shared GND
  LEDs wired to pins D2 - D5 via 220Ω resistor, and shared GND
  DY-SV5W Serial Audio Player
  Speaker
  Correct and Incorrect buttons
  5V DC

custom parts:
  Arcade Button (red): Adafruit Arcade Button (red)
  Arcade Button (blue): Adafruit Arcade Button (blue)
  Arcade Button (green): Adafruit Arcade Button (green)
  Arcade Button (yellow): Adafruit Arcade Button (yellow)
